# Fritzing sketch pi schematic (saved by Fritzing 0.9.3b)
breadboards: 1

parts:
  R2 = Resistor [tolerance=±5% resistance=100 package=THT]
  R3 = Resistor [tolerance=±5% resistance=100 package=THT]
  LED2 = LED - 5mm [color="Red (633nm)" package="5 mm [THT]"]
  R1 = Resistor [tolerance=±5% resistance=100 package=THT]
  LED3 = LED - 5mm [color="Red (633nm)" package="5 mm [THT]"]
  LED1 = LED - 5mm [color="Red (633nm)" package="5 mm [THT]"]
  Raspberry_Pi_1 = Raspberry Pi 3 [part_number=RPI-3-V1.2]
  S1 = Round Pushbutton

nets:
  N1: R2.Pin_1, LED2.anode
  N2: R3.Pin_1, LED3.anode
  N3: LED2.cathode, Raspberry_Pi_1.GPIO16
  N4: R1.Pin_0, Raspberry_Pi_1.GND, S1.leg0
  N5: R1.Pin_1, LED1.anode
  N6: LED3.cathode, Raspberry_Pi_1.GPIO20
  N7: LED1.cathode, Raspberry_Pi_1.GPIO12
  N8: Raspberry_Pi_1.GPIO21, S1.leg1
